// Logisim project TP1 archi.circ as structural Verilog: 2 circuits, main circuit main
module main (
);

  _7_Segment_Display u_7_segment_display_1 ();  // open: g, f, a, b, e, d, c, dp
endmodule

module affichage_7 (
  input  A,
  input  B,
  input  C,
  input  D
);

  wire and_1_out, and_2_out, and_3_out, and_4_out, and_5_out, and_6_out, and_7_out, or_1_out, or_2_out,
       or_3_out, or_4_out, or_5_out, or_6_out, or_7_out, or_8_out, or_9_out, or_10_out, or_11_out, or_12_out,
       xnor_1_out, xnor_2_out;

  and and_1 (and_1_out, C, ~A);  // AND_Gate
  and and_2 (and_2_out, ~C, ~A);  // AND_Gate
  and and_3 (and_3_out, ~C, A);  // AND_Gate
  and and_4 (and_4_out, A, ~A);  // AND_Gate
  or or_1 (or_1_out, and_2_out, and_3_out);
  and and_5 (and_5_out, and_1_out, A);
  or or_2 (or_2_out, or_1_out, and_4_out);
  or or_3 (or_3_out, and_5_out, D);
  or or_4 (or_4_out, or_2_out, or_3_out);
  or or_5 (or_5_out, A, A);
  or or_6 (or_6_out, D, ~C);  // OR_Gate
  and and_6 (and_6_out, ~A, ~D);  // AND_Gate
  and and_7 (and_7_out, C, ~D);  // AND_Gate
  or or_7 (or_7_out, A, C);
  or or_8 (or_8_out, A, ~A);  // OR_Gate
  xnor xnor_1 (xnor_1_out, C, D);
  xnor xnor_2 (xnor_2_out, A, D);
  or or_9 (or_9_out, and_6_out, and_7_out);
  or or_10 (or_10_out, or_8_out, xnor_1_out);
  or or_11 (or_11_out, or_5_out, or_6_out);
  or or_12 (or_12_out, or_7_out, xnor_2_out);
  _7_Segment_Display u_7_segment_display_1 (
    .a(or_12_out), .b(or_10_out), .e(or_9_out), .d(or_4_out), .c(or_11_out));  // open: g, f, dp

  assign B = A;
endmodule
