// Logisim project test.circ as structural Verilog: 5 circuits, main circuit main
module main (
  input  A,
  input  A_2,
  input  B,
  input  B_2,
  input  C,
  input  C_2,
  input  D,
  input  D_2,
  input  Com,
  output D_3
);

  wire add_sous_4bit_1_s0, add_sous_4bit_1_s1, add_sous_4bit_1_s2, add_sous_4bit_1_s3;
  wire [6:0] affichage_7_1_out_5, affichage_7_2_out_5, affichage_7_3_out_5;

  affichage_7 affichage_7_1 (.A(A), .B(B), .C(C), .D(D), .out_5(affichage_7_1_out_5));
  add_sous_4bit add_sous_4bit_1 (
    .a2(B), .a3(A), .a0(D), .a1(C), .b2(B_2), .b3(A_2), .b0(D_2), .b1(C_2), .com(Com),
    .s2(add_sous_4bit_1_s2), .s3(add_sous_4bit_1_s3), .s0(add_sous_4bit_1_s0), .s1(add_sous_4bit_1_s1),
    .D(D_3));
  _7_Segment_Display u_7_segment_display_1 (
    .g(affichage_7_1_out_5[6]), .f(affichage_7_1_out_5[5]), .a(affichage_7_1_out_5[0]),
    .b(affichage_7_1_out_5[1]), .e(affichage_7_1_out_5[4]), .d(affichage_7_1_out_5[3]),
    .c(affichage_7_1_out_5[2]));  // open: dp
  affichage_7 affichage_7_2 (
    .A(add_sous_4bit_1_s3), .B(add_sous_4bit_1_s2), .C(add_sous_4bit_1_s1), .D(add_sous_4bit_1_s0),
    .out_5(affichage_7_2_out_5));
  affichage_7 affichage_7_3 (.A(A_2), .B(B_2), .C(C_2), .D(D_2), .out_5(affichage_7_3_out_5));
  _7_Segment_Display u_7_segment_display_2 (
    .g(affichage_7_2_out_5[6]), .f(affichage_7_2_out_5[5]), .a(affichage_7_2_out_5[0]),
    .b(affichage_7_2_out_5[1]), .e(affichage_7_2_out_5[4]), .d(affichage_7_2_out_5[3]),
    .c(affichage_7_2_out_5[2]));  // open: dp
  _7_Segment_Display u_7_segment_display_3 (
    .g(affichage_7_3_out_5[6]), .f(affichage_7_3_out_5[5]), .a(affichage_7_3_out_5[0]),
    .b(affichage_7_3_out_5[1]), .e(affichage_7_3_out_5[4]), .d(affichage_7_3_out_5[3]),
    .c(affichage_7_3_out_5[2]));  // open: dp
endmodule

module affichage_7 (
  input  A,
  input  B,
  input  C,
  input  D,
  output [6:0] out_5
);

  wire and_1_out, and_2_out, and_3_out, and_4_out, and_5_out, and_6_out, and_7_out, nand_1_out, nor_1_out,
       nor_2_out, or_1_out, or_2_out, or_3_out, xnor_1_out, xnor_2_out, xor_1_out;

  or u_a (out_5[0], A, C, xnor_1_out);
  xnor xnor_1 (xnor_1_out, D, B);
  nor nor_1 (nor_1_out, A, B);
  or u_b (out_5[1], A, nor_1_out, xnor_2_out);
  xnor xnor_2 (xnor_2_out, D, C);
  or u_c (out_5[2], D, ~C, B, A);  // OR_Gate
  and and_1 (and_1_out, ~B, or_1_out);  // AND_Gate
  or u_d (out_5[3], A, and_1_out, and_2_out, and_3_out);
  or or_1 (or_1_out, C, ~D);  // OR_Gate
  and and_2 (and_2_out, C, ~D);  // AND_Gate
  and and_3 (and_3_out, D, B, ~C);  // AND_Gate
  or or_2 (or_2_out, C, B);
  and and_4 (and_4_out, A, or_2_out);
  and and_5 (and_5_out, ~D, or_3_out);  // AND_Gate
  or e (out_5[4], and_4_out, and_5_out);
  or or_3 (or_3_out, C, ~B);  // OR_Gate
  and and_6 (and_6_out, B, nand_1_out);
  or f (out_5[5], A, and_6_out, nor_2_out);
  nand nand_1 (nand_1_out, D, C);
  nor nor_2 (nor_2_out, D, C);
  and and_7 (and_7_out, C, ~D);  // AND_Gate
  xor xor_1 (xor_1_out, B, C);
  or g (out_5[6], and_7_out, xor_1_out, A);
endmodule

module _1_2 (
  input  A,
  input  B,
  input  C,
  output S,
  output Rs
);

  wire xor_2_out;

  xor xor_1 (S, A, B);
  xor xor_2 (xor_2_out, A, C);
  and and_1 (Rs, B, xor_2_out);
endmodule

module add_sous (
  input  Re,
  input  A,
  input  B,
  input  C,
  output S,
  output Rs
);

  wire n1_2_1_rs, n1_2_1_s, n1_2_2_rs;

  _1_2 u_1_2_1 (.A(A), .B(B), .C(C), .S(n1_2_1_s), .Rs(n1_2_1_rs));
  _1_2 u_1_2_2 (.A(n1_2_1_s), .B(Re), .C(C), .S(S), .Rs(n1_2_2_rs));
  or or_1 (Rs, n1_2_2_rs, n1_2_1_rs);
endmodule

module add_sous_4bit (
  input  a2,
  input  a3,
  input  a0,
  input  a1,
  input  b2,
  input  b3,
  input  b0,
  input  b1,
  input  com,
  output s2,
  output s3,
  output s0,
  output s1,
  output D
);

  wire add_sous_1_rs, add_sous_2_rs, add_sous_3_rs;

  add_sous add_sous_1 (.Re(1'b0), .A(a0), .B(b0), .C(com), .S(s0), .Rs(add_sous_1_rs));
  add_sous add_sous_2 (.Re(add_sous_1_rs), .A(a1), .B(b1), .C(com), .S(s1), .Rs(add_sous_2_rs));
  add_sous add_sous_3 (.Re(add_sous_2_rs), .A(a2), .B(b2), .C(com), .S(s2), .Rs(add_sous_3_rs));
  add_sous add_sous_4 (.Re(add_sous_3_rs), .A(a3), .B(b3), .C(com), .S(s3), .Rs(D));
endmodule
